// Logisim project exercise3.circ as structural Verilog: 1 circuit, main circuit main
module main (
  input  in_1,
  input  in_2,
  input  in_3,
  input  in_4,
  input  in_5,
  input  in_6
);

  wire Somador_3_bits_a0, Somador_3_bits_a1, Somador_3_bits_a2;

  somador_3bits_main Somador_3_bits (
    .in_5(in_4), .in_6(in_1), .A0(Somador_3_bits_a0), .in_3(in_5), .in_4(in_2), .A1(Somador_3_bits_a1),
    .in_1(in_6), .in_2(in_3), .A2(Somador_3_bits_a2));  // open: CO
  // registrador_3flip_main Registrador_3_bits: pin names not known; wires that end beside it: Somador_3_bits_a2, Somador_3_bits_a1, Somador_3_bits_a0
  _7_Segment_Display u_7_segment_display_1 ();  // open: g, f, a, b, e, d, c, dp
endmodule
