// Logisim project full-adder-3bits.circ as structural Verilog: 1 circuit, main circuit main
module main (
  input  A,
  input  B,
  input  CI,
  output S,
  output CO
);

  wire and_1_out, and_2_out, xor_1_out;

  xor xor_1 (xor_1_out, A, B);
  and and_1 (and_1_out, CI, xor_1_out);
  and and_2 (and_2_out, B, A);
  xor xor_2 (S, xor_1_out, CI);
  or or_1 (CO, and_1_out, and_2_out);
endmodule
