// Logisim project half-adder-3bits.circ as structural Verilog: 1 circuit, main circuit main
module main (
  input  A,
  input  B,
  output S,
  output CO
);

  xor xor_1 (S, B, A);
  and and_1 (CO, A, B);
endmodule
