// Logisim project somador-3bits.circ as structural Verilog: 1 circuit, main circuit main
module main (
  input  in_1,
  input  in_2,
  input  in_3,
  input  in_4,
  input  in_5,
  input  in_6,
  output A0,
  output CO,
  output A2,
  output A1
);

  wire main_2_co, main_3_co;

  full_adder_3bits_main main_1 (.A(in_2), .B(in_1), .CI(main_2_co), .S(A2), .CO(CO));
  full_adder_3bits_main main_2 (.A(in_4), .B(in_3), .CI(main_3_co), .S(A1), .CO(main_2_co));
  half_adder_3bits_main main_3 (.A(in_6), .B(in_5), .S(A0), .CO(main_3_co));
endmodule
